// Logisim project s-mips-lib.circ as structural Verilog: 1 circuit, main circuit Register File
module Register_File (
  input  Read_Write,
  input  [4:0] in_2,
  input  [31:0] in_3,
  input  [4:0] in_4,
  input  [4:0] in_5,
  input  in_6,
  input  in_7,
  output [31:0] A,
  output [31:0] B
);

  wire E0, E1, E2, E3, E4, E5, E6, E7, E8, E9, E10, E11, E12, E13, E14, E15, E16, E17, E18, E19, E20, E21,
       E22, E23, E24, E25, E26, E27, E28, E29, E30, E31;
  wire [31:0] Q0, Q1, Q2, Q3, Q4, Q5, Q6, Q7, Q8, Q9, Q10, Q11, Q12, Q13, Q14, Q15, Q16, Q17, Q18, Q19, Q20,
       Q21, Q22, Q23, Q24, Q25, Q26, Q27, Q28, Q29, Q30, Q31;

  Decoder #(.select(5)) decoder_1 (
    .out0(E0), .out1(E1), .out2(E2), .out3(E3), .out4(E4), .out5(E5), .out6(E6), .out7(E7), .out8(E8),
    .out9(E9), .out10(E10), .out11(E11), .out12(E12), .out13(E13), .out14(E14), .out15(E15), .out16(E16),
    .out17(E17), .out18(E18), .out19(E19), .out20(E20), .out21(E21), .out22(E22), .out23(E23), .out24(E24),
    .out25(E25), .out26(E26), .out27(E27), .out28(E28), .out29(E29), .out30(E30), .out31(E31), .sel(in_2),
    .en(Read_Write));
  Register #(.width(32)) register_1 (.D({32{1'b0}}), .en(E0), .Q(Q0), .clk(in_6), .clr(in_7));
  Register #(.width(32)) register_2 (.D(in_3), .en(E1), .Q(Q1), .clk(in_6), .clr(in_7));
  Register #(.width(32)) register_3 (.D(in_3), .en(E2), .Q(Q2), .clk(in_6), .clr(in_7));
  Register #(.width(32)) register_4 (.D(in_3), .en(E3), .Q(Q3), .clk(in_6), .clr(in_7));
  Register #(.width(32)) register_5 (.D(in_3), .en(E4), .Q(Q4), .clk(in_6), .clr(in_7));
  Register #(.width(32)) register_6 (.D(in_3), .en(E5), .Q(Q5), .clk(in_6), .clr(in_7));
  Register #(.width(32)) register_7 (.D(in_3), .en(E6), .Q(Q6), .clk(in_6), .clr(in_7));
  Register #(.width(32)) register_8 (.D(in_3), .en(E7), .Q(Q7), .clk(in_6), .clr(in_7));
  Register #(.width(32)) register_9 (.D(in_3), .en(E8), .Q(Q8), .clk(in_6), .clr(in_7));
  Register #(.width(32)) register_10 (.D(in_3), .en(E9), .Q(Q9), .clk(in_6), .clr(in_7));
  Register #(.width(32)) register_11 (.D(in_3), .en(E10), .Q(Q10), .clk(in_6), .clr(in_7));
  Register #(.width(32)) register_12 (.D(in_3), .en(E11), .Q(Q11), .clk(in_6), .clr(in_7));
  Register #(.width(32)) register_13 (.D(in_3), .en(E12), .Q(Q12), .clk(in_6), .clr(in_7));
  Register #(.width(32)) register_14 (.D(in_3), .en(E13), .Q(Q13), .clk(in_6), .clr(in_7));
  Register #(.width(32)) register_15 (.D(in_3), .en(E14), .Q(Q14), .clk(in_6), .clr(in_7));
  Register #(.width(32)) register_16 (.D(in_3), .en(E15), .Q(Q15), .clk(in_6), .clr(in_7));
  Register #(.width(32)) register_17 (.D(in_3), .en(E16), .Q(Q16), .clk(in_6), .clr(in_7));
  Register #(.width(32)) register_18 (.D(in_3), .en(E17), .Q(Q17), .clk(in_6), .clr(in_7));
  Register #(.width(32)) register_19 (.D(in_3), .en(E18), .Q(Q18), .clk(in_6), .clr(in_7));
  Register #(.width(32)) register_20 (.D(in_3), .en(E19), .Q(Q19), .clk(in_6), .clr(in_7));
  Register #(.width(32)) register_21 (.D(in_3), .en(E20), .Q(Q20), .clk(in_6), .clr(in_7));
  Register #(.width(32)) register_22 (.D(in_3), .en(E21), .Q(Q21), .clk(in_6), .clr(in_7));
  Register #(.width(32)) register_23 (.D(in_3), .en(E22), .Q(Q22), .clk(in_6), .clr(in_7));
  Register #(.width(32)) register_24 (.D(in_3), .en(E23), .Q(Q23), .clk(in_6), .clr(in_7));
  Register #(.width(32)) register_25 (.D(in_3), .en(E24), .Q(Q24), .clk(in_6), .clr(in_7));
  Register #(.width(32)) register_26 (.D(in_3), .en(E25), .Q(Q25), .clk(in_6), .clr(in_7));
  Register #(.width(32)) register_27 (.D(in_3), .en(E26), .Q(Q26), .clk(in_6), .clr(in_7));
  Register #(.width(32)) register_28 (.D(in_3), .en(E27), .Q(Q27), .clk(in_6), .clr(in_7));
  Register #(.width(32)) register_29 (.D(in_3), .en(E28), .Q(Q28), .clk(in_6), .clr(in_7));
  Register #(.width(32)) register_30 (.D(in_3), .en(E29), .Q(Q29), .clk(in_6), .clr(in_7));
  Register #(.width(32)) register_31 (.D(in_3), .en(E30), .Q(Q30), .clk(in_6), .clr(in_7));
  Register #(.width(32)) register_32 (.D(in_3), .en(E31), .Q(Q31), .clk(in_6), .clr(in_7));
  Multiplexer #(.select(5), .width(32), .enable("false")) multiplexer_1 (
    .in0(Q0), .in1(Q1), .in2(Q2), .in3(Q3), .in4(Q4), .in5(Q5), .in6(Q6), .in7(Q7), .in8(Q8), .in9(Q9),
    .in10(Q10), .in11(Q11), .in12(Q12), .in13(Q13), .in14(Q14), .in15(Q15), .in16(Q16), .in17(Q17),
    .in18(Q18), .in19(Q19), .in20(Q20), .in21(Q21), .in22(Q22), .in23(Q23), .in24(Q24), .in25(Q25),
    .in26(Q26), .in27(Q27), .in28(Q28), .in29(Q29), .in30(Q30), .in31(Q31), .out(A), .sel(in_4));
  Multiplexer #(.select(5), .width(32), .enable("false")) multiplexer_2 (
    .in0(Q0), .in1(Q1), .in2(Q2), .in3(Q3), .in4(Q4), .in5(Q5), .in6(Q6), .in7(Q7), .in8(Q8), .in9(Q9),
    .in10(Q10), .in11(Q11), .in12(Q12), .in13(Q13), .in14(Q14), .in15(Q15), .in16(Q16), .in17(Q17),
    .in18(Q18), .in19(Q19), .in20(Q20), .in21(Q21), .in22(Q22), .in23(Q23), .in24(Q24), .in25(Q25),
    .in26(Q26), .in27(Q27), .in28(Q28), .in29(Q29), .in30(Q30), .in31(Q31), .out(B), .sel(in_5));

  // Other names for the same wires on the sheet: clk = in_6; DA[4:0] = in_2; DI[31:0] = in_3; reset = in_7;
  //   RW = Read_Write; SA[4:0] = in_4; SB[4:0] = in_5

  // Notes on the sheet:
  //   INPUT
  //   OUTPUT
endmodule
